# Fritzing sketch esquematico (saved by Fritzing 0.9.3b)
breadboards: 1

parts:
  8x8_LED_Modul_mit_MAX1 = 8x8 LED Modul mit MAX7219 [package=THT]
  S1 = Pushbutton [package="[THT]"]
  S2 = Pushbutton [package="[THT]"]
  S3 = Pushbutton [package="[THT]"]
  S4 = Pushbutton [package="[THT]"]
  Componente1 = Arduino Uno (Rev3) - ICSP

nets:
  N1: 8x8_LED_Modul_mit_MAX1.VCC_Eingang, Componente1.5V
  N2: 8x8_LED_Modul_mit_MAX1.GND_Eingang, S1.Pin_1, S1.Pin_2, S2.Pin_1, S2.Pin_2, S3.Pin_1, S3.Pin_2, S4.Pin_1, S4.Pin_2, Componente1.GND
  N3: 8x8_LED_Modul_mit_MAX1.DIN_Eingang, Componente1.D12/MISO
  N4: 8x8_LED_Modul_mit_MAX1.CS_Eingang, Componente1.D10_PWM/SS
  N5: 8x8_LED_Modul_mit_MAX1.CLK_Eingang, Componente1.D11_PWM/MOSI
  N6: S1.Pin_3, S1.Pin_4, Componente1.D3_PWM
  N7: S2.Pin_3, S2.Pin_4, Componente1.D4
  N8: S3.Pin_3, S3.Pin_4, Componente1.D5_PWM
  N9: S4.Pin_3, S4.Pin_4, Componente1.D6_PWM
